// Digital circuit lab06.dig as structural Verilog
module lab06 (
  input  [4:0] RR0,
  input  [4:0] RR1,
  input  WE,
  input  [4:0] WR,
  input  CLR,
  input  [1:0] PROG,
  input  CLK,
  input  [2:0] ALUOp,
  input  ALUSrcB,
  input  [63:0] Imm,
  output [63:0] T0,
  output [63:0] T1
);

  wire IW, register_file_1_p3, register_file_1_p7, x0, x1, x2, x3, x4, x7, x8, x9, x10, x11, x12, x13, x14,
       x15, x16, x17, x18, x19, x26, x27;
  wire [63:0] _64_bit_register_1_p1, _64_bit_register_1_p5, multiplexer_1_out, register_file_1_p8;

  // _64_bit_register _64_bit_register_1: pin names not known; wires that end beside it: _64_bit_register_1_p1, CLR, 1'b1, CLK, _64_bit_register_1_p5
  // instruction_memeory instruction_memeory_1: pin names not known; wires that end beside it: _64_bit_register_1_p5[7:0], PROG, IW, CLR, x26, x27
  Add #(.Bits(64)) add_1 (.a(_64_bit_register_1_p5), .b(64'h4), .c_i(1'b0), .s(_64_bit_register_1_p1));  // open: c_o
  // register_file register_file_1: pin names not known; wires that end beside it: RR0, RR1, register_file_1_p3, WE, WR, CLK, register_file_1_p7, register_file_1_p8, x0, x1, x2, x3, x4, T0, T1, x7, x8, x9, x10, x11, x12, x13, x14, x15, x16, x17, x18, x19
  Multiplexer #(.Bits(64)) multiplexer_1 (
    .sel(ALUSrcB), .in_0(register_file_1_p8), .in_1(Imm), .out(multiplexer_1_out));
  // alu alu_1: pin names not known; wires that end beside it: register_file_1_p7, multiplexer_1_out, ALUOp, register_file_1_p3

  // Other names for the same wires on the sheet: x5[63:0] = T0; x6[63:0] = T1
endmodule
